// Logisim project cache.circ as structural Verilog: 3 circuits, main circuit cache_entry
module main (
  input  [7:0] address,
  input  clock,
  input  mem_read,
  input  [31:0] write_data,
  input  mem_write,
  output [7:0] data_out
);

  wire bloco_0_miss, bloco_1_miss, bloco_2_miss, bloco_3_miss, delay_ram_2_carry, miss, not_1_out, or_1_out,
       or_2_out, s_0, s_1, s_2, s_3;
  wire [7:0] bloco_0_data_out, bloco_1_data_out, bloco_2_data_out, bloco_3_data_out;
  wire [31:0] delay_ram_q, multiplexer_1_out, ram_1_data;

  decod_and decod_and (.clock(clock), .index(address[3:2]), .s_0(s_0), .s_1(s_1), .s_2(s_2), .s_3(s_3));
  cache_entry bloco_0 (
    .data_in(multiplexer_1_out), .tag(address[7:4]), .byte_offset(address[1:0]), .clock(s_0),
    .enable(or_1_out), .data_out(bloco_0_data_out), .miss(bloco_0_miss));
  cache_entry bloco_1 (
    .data_in(multiplexer_1_out), .tag(address[7:4]), .byte_offset(address[1:0]), .clock(s_1),
    .enable(or_1_out), .data_out(bloco_1_data_out), .miss(bloco_1_miss));
  cache_entry bloco_2 (
    .data_in(multiplexer_1_out), .tag(address[7:4]), .byte_offset(address[1:0]), .clock(s_2),
    .enable(or_1_out), .data_out(bloco_2_data_out), .miss(bloco_2_miss));
  cache_entry bloco_3 (
    .data_in(multiplexer_1_out), .tag(address[7:4]), .byte_offset(address[1:0]), .clock(s_3),
    .enable(or_1_out), .data_out(bloco_3_data_out), .miss(bloco_3_miss));
  or or_1 (or_1_out, delay_ram_2_carry, mem_write);
  Multiplexer #(.width(32), .enable("false")) multiplexer_1 (
    .in0(delay_ram_q), .in1(write_data), .out(multiplexer_1_out), .sel(mem_write));
  Multiplexer #(.select(2), .width(8), .enable("false")) multiplexer_2 (
    .in0(bloco_0_data_out), .in1(bloco_1_data_out), .in2(bloco_2_data_out), .in3(bloco_3_data_out),
    .out(data_out), .sel(address[3:2]));
  Register #(.width(32)) delay_ram (.D(ram_1_data), .Q(delay_ram_q), .clk(delay_ram_2_carry));  // open: en, clr
  Multiplexer #(.select(2), .enable("false")) multiplexer_3 (
    .in0(bloco_0_miss), .in1(bloco_1_miss), .in2(bloco_2_miss), .in3(bloco_3_miss), .out(miss),
    .sel(address[3:2]));
  or or_2 (or_2_out, mem_write, miss);
  RAM #(.addrWidth(6), .dataWidth(32), .bus("separate")) ram_1 (
    .addr(address[7:2]), .din(write_data), .data(ram_1_data), .str(mem_write), .sel(or_2_out), .clk(clock),
    .ld(mem_read));  // open: clr
  not not_1 (not_1_out, miss);
  Counter #(.width(4), .max('h9)) delay_ram_2 (
    .carry(delay_ram_2_carry), .clk(clock), .clr(not_1_out));  // open: load, D, count, Q

  // Other names for the same wires on the sheet: offset[1:0] = address[1:0]; index[1:0] = address[3:2];
  //   ram_addr[5:0] = address[7:2]; tag[3:0] = address[7:4]

  // Notes on the sheet:
  //   clock + decodificador
  //   sel. escrita na cache
  //   sel. saida cache
  //   miss na cache
  //   memoria principal
endmodule

module cache_entry (
  input  [31:0] data_in,
  input  [3:0] tag,
  input  [1:0] byte_offset,
  input  clock,
  input  enable,
  output [7:0] data_out,
  output miss
);

  wire and_1_out, comparator_1_eq, valid_q;
  wire [3:0] tag_q;
  wire [7:0] byte_0_q, byte_1_q, byte_2_q, byte_3_q;

  Register byte_0 (.D(data_in[7:0]), .en(and_1_out), .Q(byte_0_q), .clk(clock));  // open: clr
  Register byte_1 (.D(data_in[15:8]), .en(and_1_out), .Q(byte_1_q), .clk(clock));  // open: clr
  Register byte_2 (.D(data_in[23:16]), .en(and_1_out), .Q(byte_2_q), .clk(clock));  // open: clr
  Register byte_3 (.D(data_in[31:24]), .en(and_1_out), .Q(byte_3_q), .clk(clock));  // open: clr
  Multiplexer #(.select(2), .width(8), .enable("false")) multiplexer_1 (
    .in0(byte_0_q), .in1(byte_1_q), .in2(byte_2_q), .in3(byte_3_q), .out(data_out), .sel(byte_offset));
  Register #(.width(4)) u_tag (.D(tag), .en(and_1_out), .Q(tag_q), .clk(clock));  // open: clr
  and and_1 (and_1_out, enable, miss);
  Comparator #(.width(4)) comparator_1 (.a(tag), .b(tag_q), .eq(comparator_1_eq));  // open: gt, lt
  Register #(.width(1)) valid (.D(and_1_out), .en(enable), .Q(valid_q), .clk(clock));  // open: clr
  nand nand_1 (miss, valid_q, comparator_1_eq);
endmodule

module decod_and (
  input  clock,
  input  [1:0] index,
  output s_0,
  output s_1,
  output s_2,
  output s_3
);

  wire decoder_1_out0, decoder_1_out1, decoder_1_out2, decoder_1_out3;

  Decoder #(.select(2), .disabled(0), .enable("false")) decoder_1 (
    .out0(decoder_1_out0), .out1(decoder_1_out1), .out2(decoder_1_out2), .out3(decoder_1_out3), .sel(index));
  and and_1 (s_0, decoder_1_out0, clock);
  and and_2 (s_1, decoder_1_out1, clock);
  and and_3 (s_2, decoder_1_out2, clock);
  and and_4 (s_3, decoder_1_out3, clock);
endmodule
